// Logisim project MyRISCV.circ as structural Verilog: 11 circuits, main circuit main
// IDEC
module Instruction_Decoder (
  input  [31:0] instruction,
  output [6:0] opcode,
  output [4:0] rd,
  output [2:0] funct3,
  output [4:0] rs1,
  output [4:0] rs2,
  output [6:0] funct7,
  output [31:0] immediate
);

  Immediate_Generator immediate_generator_1 (.instruction(instruction), .immediate(immediate));

  assign funct3 = instruction[14:12];
  assign funct7 = instruction[31:25];
  assign opcode = instruction[6:0];
  assign rd = instruction[11:7];
  assign rs1 = instruction[19:15];
  assign rs2 = instruction[24:20];

  // Other names for the same wires on the sheet: I[31:0] = instruction; OP[6:0] = instruction[6:0];
  //   F3[2:0] = instruction[14:12]; F7[6:0] = instruction[31:25]; IMM[31:0] = immediate
endmodule

// IMM_GEN
module Immediate_Generator (
  input  [31:0] instruction,
  output [31:0] immediate
);

  wire and_3_out, and_4_out, and_5_out, and_7_out, and_8_out, CAT0, CAT1, CAT2, CAT3, CAT4, CAT5, CAT6, CAT7,
       is_B, is_I, is_I_0, is_I_2, is_I_or_J, is_I_or_S, is_J, is_J_or_U, is_S, is_S_or_B, not_1_out;
  wire [3:0] and_1_out, and_2_out, bit_extender_1_out, bit_extender_2_out;
  wire [5:0] bit_extender_4_out;
  wire [7:0] bit_extender_5_out;
  wire [10:0] bit_extender_3_out;

  or or_1 (is_S_or_B, is_S, is_B);
  nor nor_1 (is_I_or_S, is_B, is_J, CAT5);
  assign bit_extender_1_out = {{3{is_I_or_J}}, is_I_or_J};  // Bit_Extender bit_extender_1
  assign bit_extender_2_out = {{3{is_S_or_B}}, is_S_or_B};  // Bit_Extender bit_extender_2
  assign bit_extender_3_out = {{10{instruction[31]}}, instruction[31]};  // Bit_Extender bit_extender_3
  Multiplexer #(.width(11)) multiplexer_1 (
    .in0(bit_extender_3_out), .in1(instruction[30:20]), .out(immediate[30:20]), .sel(CAT5));
  Decoder #(.enable("false"), .select(3)) decoder_1 (
    .out0(CAT0), .out1(CAT1), .out2(CAT2), .out3(CAT3), .out4(CAT4), .out5(CAT5), .out6(CAT6), .out7(CAT7),
    .sel(instruction[4:2]));
  assign and_1_out = bit_extender_1_out & instruction[24:21];  // AND_Gate and_1, 4 bits wide
  assign and_2_out = bit_extender_2_out & instruction[11:8];  // AND_Gate and_2, 4 bits wide
  assign immediate[4:1] = and_1_out | and_2_out;  // OR_Gate or_2, 4 bits wide
  or or_3 (is_J_or_U, is_J, CAT5);
  not not_1 (not_1_out, CAT5);
  and and_3 (and_3_out, is_I_or_S, instruction[31]);
  and and_4 (and_4_out, is_B, instruction[7]);
  and and_5 (and_5_out, is_J, instruction[20]);
  Decoder #(.select(2)) decoder_2 (
    .out0(is_I_0), .out1(is_S), .out3(is_B), .sel(instruction[6:5]), .en(CAT0));  // open: out2
  or or_4 (is_I, is_I_0, CAT1, is_I_2, CAT4);
  assign bit_extender_4_out = {{5{not_1_out}}, not_1_out};  // Bit_Extender bit_extender_4
  assign immediate[10:5] = bit_extender_4_out & instruction[30:25];  // AND_Gate and_6, 6 bits wide
  or or_5 (immediate[11], and_3_out, and_4_out, and_5_out);
  and and_7 (and_7_out, instruction[20], is_I);
  and and_8 (and_8_out, instruction[7], is_S);
  Decoder #(.select(2)) decoder_3 (.out0(is_I_2), .out3(is_J), .sel(instruction[6:5]), .en(CAT3));  // open: out1, out2
  or or_6 (immediate[0], and_7_out, and_8_out);
  nor nor_2 (is_I_or_J, is_S, is_B, CAT5);
  assign bit_extender_5_out = {{7{instruction[31]}}, instruction[31]};  // Bit_Extender bit_extender_5
  Multiplexer #(.width(8)) multiplexer_2 (
    .in0(bit_extender_5_out), .in1(instruction[19:12]), .out(immediate[19:12]), .sel(is_J_or_U));

  assign immediate[31] = instruction[31];

  // Other names for the same wires on the sheet: I[31:0] = instruction; LEN[1:0] = instruction[1:0];
  //   CAT[2:0] = instruction[4:2]; VAR[1:0] = instruction[6:5]; is_I_1 = CAT1; is_I_3 = CAT4; is_U = CAT5;
  //   RET[31:0] = {instruction[31], immediate[30:0]}; SEG0 = immediate[0]; SEG1[3:0] = immediate[4:1];
  //   SEG2[5:0] = immediate[10:5]; SEG3 = immediate[11]; SEG4[7:0] = immediate[19:12]; SEG5[10:0] = immediate[30:20];
  //   SEG6 = instruction[31]
endmodule

module main (
  input  CLK
);

  wire alu_controller_1_is_r, alu_controller_1_special_bit, pc_controller_1_pc_clk, pc_controller_1_we,
       ram_controller_1_ram_clk, ram_controller_1_ram_output_enable, ram_controller_1_ram_write_enable,
       REG_WE, S_CTRL, S_DECODE, S_EXEC, S_EXEC_WB, S_FETCH, S_LOAD_WB, S_MEM, sr_controller_1_sr_clk,
       sr_controller_1_we;
  wire [2:0] alu_controller_1_funct3, funct3, ram_controller_1_ram_funct3, SR, sr_controller_1_next_state;
  wire [4:0] rd, rs1, rs2;
  wire [6:0] funct7, opcode;
  wire [31:0] alu_controller_1_a, alu_controller_1_b, ALU_result, ALUOut, curr_pc, immediate, IR, MDR, pc,
       pc_controller_1_new_pc, ram_controller_1_ram_address, ram_controller_1_ram_write_data, RAM_output,
       Register_File_write_data, rs1_data, rs2_data;

  Register #(.width(32)) u_pc (
    .D(pc_controller_1_new_pc), .en(pc_controller_1_we), .clk(pc_controller_1_pc_clk), .Q(pc));  // open: clr
  PC_Controller pc_controller_1 (
    .is_fetch(S_FETCH), .is_control(S_CTRL), .opcode(opcode), .funct3(funct3), .rs1_data(rs1_data),
    .rs2_data(rs2_data), .immediate(immediate), .pc(pc), .CLK(CLK), .new_pc(pc_controller_1_new_pc),
    .WE(pc_controller_1_we), .pc_CLK(pc_controller_1_pc_clk));
  SR_Controller sr_controller_1 (
    .SR(SR), .RAM_output(RAM_output), .opcode(opcode), .CLK(CLK), .next_state(sr_controller_1_next_state),
    .WE(sr_controller_1_we), .SR_CLK(sr_controller_1_sr_clk));
  Instruction_Decoder instruction_decoder_1 (
    .instruction(IR), .opcode(opcode), .rd(rd), .funct3(funct3), .rs1(rs1), .rs2(rs2), .funct7(funct7),
    .immediate(immediate));
  Register #(.width(3)) u_SR (
    .D(sr_controller_1_next_state), .en(sr_controller_1_we), .clk(sr_controller_1_sr_clk), .Q(SR));  // open: clr
  Register_File register_file_1 (
    .write_enable(REG_WE), .write_address(rd), .output_address_0(rs1), .output_address_1(rs2),
    .write_data(Register_File_write_data), .CLK(CLK), .output_data_0(rs1_data), .output_data_1(rs2_data));
  ALU_Controller alu_controller_1 (
    .opcode(opcode), .funct3_in(funct3), .funct7(funct7), .rs1_data(rs1_data), .rs2_data(rs2_data),
    .immediate(immediate), .curr_pc(curr_pc), .is_R(alu_controller_1_is_r),
    .special_bit(alu_controller_1_special_bit), .funct3(alu_controller_1_funct3), .A(alu_controller_1_a),
    .B(alu_controller_1_b));
  Decoder #(.enable("false"), .select(3)) decoder_1 (
    .out0(S_FETCH), .out1(S_DECODE), .out2(S_EXEC), .out3(S_EXEC_WB), .out4(S_MEM), .out5(S_LOAD_WB),
    .out6(S_CTRL), .sel(SR));  // open: out7
  ALU alu_1 (
    .is_R(alu_controller_1_is_r), .special_bit(alu_controller_1_special_bit),
    .funct3(alu_controller_1_funct3), .A(alu_controller_1_a), .B(alu_controller_1_b), .result(ALU_result));
  Multiplexer #(.width(32)) multiplexer_1 (
    .in0({32{1'b0}}), .in1(ALU_result), .out(Register_File_write_data), .sel(opcode[4]));
  RAM_Controller ram_controller_1 (
    .S_FETCH(S_FETCH), .S_MEM(S_MEM), .opcode(opcode), .funct3(funct3), .pc(pc), .ALUOut(ALUOut),
    .rs2_data(rs2_data), .CLK(CLK), .RAM_funct3(ram_controller_1_ram_funct3),
    .RAM_output_enable(ram_controller_1_ram_output_enable),
    .RAM_write_enable(ram_controller_1_ram_write_enable), .RAM_address(ram_controller_1_ram_address),
    .RAM_write_data(ram_controller_1_ram_write_data), .RAM_CLK(ram_controller_1_ram_clk));
  Multi_Wordlen_RAM multi_wordlen_ram_1 (
    .output_enable(ram_controller_1_ram_output_enable), .write_enable(ram_controller_1_ram_write_enable),
    .address(ram_controller_1_ram_address), .write_data(ram_controller_1_ram_write_data),
    .CLK(ram_controller_1_ram_clk), .funct3(ram_controller_1_ram_funct3), .output_data(RAM_output));
  Register #(.width(32)) u_curr_pc (.D(pc), .en(S_FETCH), .clk(CLK), .Q(curr_pc));  // open: clr
  Register #(.width(32)) u_IR (.D(RAM_output), .en(S_DECODE), .clk(CLK), .Q(IR));  // open: clr
  Register #(.width(32)) u_MDR (.D(RAM_output), .en(S_MEM), .clk(CLK), .Q(MDR));  // open: clr
  Register #(.width(32)) u_ALUOut (.D(ALU_result), .en(S_EXEC), .clk(CLK), .Q(ALUOut));  // open: clr
endmodule

module ALU (
  input  is_R,
  input  special_bit,
  input  [2:0] funct3,
  input  [31:0] A,
  input  [31:0] B,
  output [31:0] result
);

  wire comparator_1_lt, comparator_2_lt, is_SUB;
  wire [31:0] ADD_or_SUB, AND_0, bit_extender_1_out, OR_0, processed_B, SLL_0, SLT, SLTU, SR, SRA_0, SRL_0,
       XOR_0;

  and and_1 (is_SUB, special_bit, is_R);
  assign bit_extender_1_out = {{31{is_SUB}}, is_SUB};  // Bit_Extender bit_extender_1
  Adder #(.width(32)) adder_1 (.a(A), .b(processed_B), .out(ADD_or_SUB), .cin(is_SUB));  // open: cout
  Shifter #(.width(32)) shifter_1 (.in(A), .\dist (B[4:0]), .out(SLL_0));
  assign processed_B = bit_extender_1_out ^ B;  // XOR_Gate xor_1, 32 bits wide
  Comparator #(.width(32)) comparator_1 (.a(A), .b(B), .lt(comparator_1_lt));  // open: gt, eq
  Comparator #(.mode("unsigned"), .width(32)) comparator_2 (.a(A), .b(B), .lt(comparator_2_lt));  // open: gt, eq
  assign XOR_0 = A ^ B;  // XOR_Gate xor_2, 32 bits wide
  Shifter #(.shift("lr"), .width(32)) shifter_2 (.in(A), .\dist (B[4:0]), .out(SRL_0));
  Shifter #(.shift("ar"), .width(32)) shifter_3 (.in(A), .\dist (B[4:0]), .out(SRA_0));
  assign SLT = {{31{1'b0}}, comparator_1_lt};  // Bit_Extender bit_extender_2
  assign SLTU = {{31{1'b0}}, comparator_2_lt};  // Bit_Extender bit_extender_3
  Multiplexer #(.width(32)) multiplexer_1 (.in0(SRL_0), .in1(SRA_0), .out(SR), .sel(special_bit));
  assign OR_0 = A | B;  // OR_Gate or_1, 32 bits wide
  assign AND_0 = A & B;  // AND_Gate and_2, 32 bits wide
  Multiplexer #(.select(3), .width(32)) multiplexer_2 (
    .in0(ADD_or_SUB), .in1(SLL_0), .in2(SLT), .in3(SLTU), .in4(XOR_0), .in5(SR), .in6(OR_0), .in7(AND_0),
    .out(result), .sel(funct3));

  // Other names for the same wires on the sheet: R = is_R; RET[31:0] = result; SB = special_bit
endmodule

module Multi_Wordlen_RAM (
  input  [2:0] funct3,
  input  output_enable,
  input  write_enable,
  input  [31:0] address,
  input  [31:0] write_data,
  input  CLK,
  output [31:0] output_data
);

  wire and_1_out, and_2_out, OE0, OE1, OE1_RAW, OE2, OE2_RAW, OE3, OE3_RAW, WE0, WE1, WE1_RAW, WE2, WE2_RAW,
       WE3, WE3_RAW;
  wire [1:0] stored_CS;
  wire [2:0] stored_F3;
  wire [7:0] OD0, OD1, OD2, OD3, WD1, WD2, WD3;
  wire [31:0] B_DATA, HW_DATA;

  Register #(.width(2)) register_1 (.D(address[1:0]), .en(1'b1), .clk(CLK), .Q(stored_CS));  // open: clr
  Decoder #(.select(2)) decoder_1 (
    .out0(OE0), .out1(OE1_RAW), .out2(OE2_RAW), .out3(OE3_RAW), .sel(address[1:0]), .en(output_enable));
  and and_1 (and_1_out, B_DATA[7], ~stored_F3[2]);  // AND_Gate
  and and_2 (and_2_out, HW_DATA[15], ~stored_F3[2]);  // AND_Gate
  Multiplexer #(.select(2)) multiplexer_1 (
    .in0(OE1_RAW), .in1(OE0), .in2(OE0), .in3(1'b0), .out(OE1), .sel(funct3[1:0]));
  Multiplexer #(.select(2)) multiplexer_2 (
    .in0(OE2_RAW), .in1(OE2_RAW), .in2(OE0), .in3(1'b0), .out(OE2), .sel(funct3[1:0]));
  Multiplexer #(.select(2)) multiplexer_3 (
    .in0(OE3_RAW), .in1(OE2_RAW), .in2(OE0), .in3(1'b0), .out(OE3), .sel(funct3[1:0]));
  assign B_DATA[31:8] = {{23{and_1_out}}, and_1_out};  // Bit_Extender bit_extender_1
  assign HW_DATA[31:16] = {{15{and_2_out}}, and_2_out};  // Bit_Extender bit_extender_2
  Register #(.width(3)) register_2 (.D(funct3), .en(1'b1), .clk(CLK), .Q(stored_F3));  // open: clr
  Decoder #(.select(2)) decoder_2 (
    .out0(WE0), .out1(WE1_RAW), .out2(WE2_RAW), .out3(WE3_RAW), .sel(address[1:0]), .en(write_enable));
  Multiplexer #(.select(2)) multiplexer_4 (
    .in0(WE1_RAW), .in1(WE0), .in2(WE0), .in3(1'b0), .out(WE1), .sel(funct3[1:0]));
  Multiplexer #(.select(2)) multiplexer_5 (
    .in0(WE2_RAW), .in1(WE2_RAW), .in2(WE0), .in3(1'b0), .out(WE2), .sel(funct3[1:0]));
  Multiplexer #(.select(2)) multiplexer_6 (
    .in0(WE3_RAW), .in1(WE2_RAW), .in2(WE0), .in3(1'b0), .out(WE3), .sel(funct3[1:0]));
  // Probe on address
  // Probe on output_data
  Multiplexer #(.select(2), .width(8)) multiplexer_7 (
    .in0(write_data[7:0]), .in1(write_data[15:8]), .in2(write_data[15:8]), .in3({8{1'b0}}), .out(WD1),
    .sel(funct3[1:0]));
  Multiplexer #(.select(2), .width(8)) multiplexer_8 (
    .in0(write_data[7:0]), .in1(write_data[7:0]), .in2(write_data[23:16]), .in3({8{1'b0}}), .out(WD2),
    .sel(funct3[1:0]));
  Multiplexer #(.select(2), .width(8)) multiplexer_9 (
    .in0(write_data[7:0]), .in1(write_data[15:8]), .in2(write_data[31:24]), .in3({8{1'b0}}), .out(WD3),
    .sel(funct3[1:0]));
  Multiplexer #(.select(2), .width(32)) multiplexer_10 (
    .in0(B_DATA), .in1(HW_DATA), .in2({OD3, OD2, OD1, OD0}), .in3({32{1'b0}}), .out(output_data),
    .sel(stored_F3[1:0]));
  RAM #(.addrWidth(24)) ram_1 (.addr(address[25:2]), .we(WE0), .oe(OE0), .clk(CLK), .din(write_data[7:0]), .dout(OD0));
  RAM #(.addrWidth(24)) ram_2 (.addr(address[25:2]), .we(WE1), .oe(OE1), .clk(CLK), .din(WD1), .dout(OD1));
  RAM #(.addrWidth(24)) ram_3 (.addr(address[25:2]), .we(WE2), .oe(OE2), .clk(CLK), .din(WD2), .dout(OD2));
  RAM #(.addrWidth(24)) ram_4 (.addr(address[25:2]), .we(WE3), .oe(OE3), .clk(CLK), .din(WD3), .dout(OD3));
  Multiplexer #(.select(2), .width(8)) multiplexer_11 (
    .in0(OD0), .in1(OD1), .in2(OD2), .in3(OD3), .out(B_DATA[7:0]), .sel(stored_CS));
  Multiplexer #(.width(16)) multiplexer_12 (
    .in0({OD1, OD0}), .in1({OD3, OD2}), .out(HW_DATA[15:0]), .sel(stored_CS[1]));

  // Other names for the same wires on the sheet: CS[1:0] = address[1:0]; A[23:0] = address[25:2];
  //   B_RAW[7:0] = B_DATA[7:0]; F3[2:0] = funct3; W[1:0] = funct3[1:0]; HW_RAW[15:0] = HW_DATA[15:0];
  //   OD[31:0] = output_data; OE = output_enable; OE0_RAW = OE0; stored_W[1:0] = stored_F3[1:0]; Z_EXT = stored_F3[2];
  //   OD_0_15[15:0] = {OD1, OD0}; W_DATA[31:0] = {OD3, OD2, OD1, OD0}; OD_16_31[15:0] = {OD3, OD2};
  //   WD[31:0] = write_data; WD0[7:0] = write_data[7:0]; WD_0_7[7:0] = write_data[7:0];
  //   WD_8_15[7:0] = write_data[15:8]; WD_16_23[7:0] = write_data[23:16]; WD_24_31[7:0] = write_data[31:24];
  //   WE = write_enable; WE0_RAW = WE0
endmodule

module ALU_Controller (
  input  [6:0] opcode,
  input  [2:0] funct3_in,
  input  [6:0] funct7,
  input  [31:0] rs1_data,
  input  [31:0] rs2_data,
  input  [31:0] immediate,
  input  [31:0] curr_pc,
  output is_R,
  output special_bit,
  output [2:0] funct3,
  output [31:0] A,
  output [31:0] B
);

  wire CAT4;
  wire [31:0] CAT5_A;

  and and_1 (CAT4, ~opcode[2], opcode[4]);  // AND_Gate
  and and_2 (is_R, opcode[5], CAT4);
  Multiplexer #(.width(3)) multiplexer_1 (.in0(3'b000), .in1(funct3_in), .out(funct3), .sel(CAT4));
  Multiplexer #(.width(32)) multiplexer_2 (.in0(curr_pc), .in1({32{1'b0}}), .out(CAT5_A), .sel(opcode[5]));
  Multiplexer #(.width(32)) multiplexer_3 (.in0(rs1_data), .in1(CAT5_A), .out(A), .sel(opcode[2]));
  Multiplexer #(.width(32)) multiplexer_4 (.in0(immediate), .in1(rs2_data), .out(B), .sel(is_R));

  assign special_bit = funct7[5];

  // Other names for the same wires on the sheet: F3[2:0] = funct3; F3_raw[2:0] = funct3_in; F7[6:0] = funct7;
  //   SB = funct7[5]; I[31:0] = immediate; OP[6:0] = opcode; CAT[2:0] = opcode[4:2]; CAT5 = opcode[2];
  //   CAT4_or_5 = opcode[4]; VAR[1:0] = opcode[6:5]; PC[31:0] = curr_pc; R = is_R; R1[31:0] = rs1_data;
  //   R2[31:0] = rs2_data
endmodule

module SR_Controller (
  input  [2:0] SR,
  input  [31:0] RAM_output,
  input  [6:0] opcode,
  input  CLK,
  output [2:0] next_state,
  output WE,
  output SR_CLK
);

  wire AUIPC, BRANCH, CAT0, CAT1, CAT2, CAT3, CAT4, CAT5, CAT6, CAT7, DECODE_next_CTRL, DECODE_next_EXEC,
       JAL, JALR, LEN_valid, LOAD, LUI, MEM_next_LOAD_WB, MISC_MEM, OP, OP_IMM, S_DECODE, STORE, SYSTEM;
  wire [1:0] LEN;
  wire [2:0] and_3_out, and_4_out, bit_extender_1_out, bit_extender_2_out, bit_extender_3_out, CAT,
       DECODE_next, EXEC_next, MEM_next;
  wire [6:5] real_O;

  Decoder #(.select(3)) decoder_1 (
    .out0(CAT0), .out1(CAT1), .out2(CAT2), .out3(CAT3), .out4(CAT4), .out5(CAT5), .out6(CAT6), .out7(CAT7),
    .sel(CAT), .en(LEN_valid));
  and and_1 (S_DECODE, SR[0], ~SR[1], ~SR[2]);  // AND_Gate
  Multiplexer #(.width(7)) multiplexer_1 (
    .in0(opcode), .in1(RAM_output[6:0]), .out({real_O, CAT, LEN}), .sel(S_DECODE));
  and and_2 (LEN_valid, LEN[0], LEN[1]);
  Decoder #(.select(2)) decoder_2 (.out0(LOAD), .out1(STORE), .out3(BRANCH), .sel(real_O), .en(CAT0));  // open: out2
  Decoder #(.select(2)) decoder_3 (.out3(JALR), .sel(real_O), .en(CAT1));  // open: out0, out1, out2
  Decoder #(.select(2)) decoder_4 (.out0(OP_IMM), .out1(OP), .out3(SYSTEM), .sel(real_O), .en(CAT4));  // open: out2
  Decoder #(.select(2)) decoder_5 (.out0(MISC_MEM), .out3(JAL), .sel(real_O), .en(CAT3));  // open: out1, out2
  Multiplexer #(.select(3), .width(3)) multiplexer_2 (
    .in0(3'b001), .in1(DECODE_next), .in2(EXEC_next), .in3(3'b000), .in4(MEM_next), .in5(3'b000),
    .in6(3'b000), .in7(3'b000), .out(next_state), .sel(SR));
  not not_1 (MEM_next_LOAD_WB, real_O[5]);
  Decoder #(.select(2)) decoder_6 (.out0(AUIPC), .out1(LUI), .sel(real_O), .en(CAT5));  // open: out2, out3
  assign and_3_out = 3'b010 & bit_extender_1_out;  // AND_Gate and_3, 3 bits wide
  assign bit_extender_1_out = {{2{DECODE_next_EXEC}}, DECODE_next_EXEC};  // Bit_Extender bit_extender_1
  assign and_4_out = 3'b110 & bit_extender_2_out;  // AND_Gate and_4, 3 bits wide
  assign bit_extender_2_out = {{2{DECODE_next_CTRL}}, DECODE_next_CTRL};  // Bit_Extender bit_extender_2
  assign bit_extender_3_out = {{2{MEM_next_LOAD_WB}}, MEM_next_LOAD_WB};  // Bit_Extender bit_extender_3
  assign DECODE_next = and_3_out | and_4_out;  // OR_Gate or_1, 3 bits wide
  assign MEM_next = 3'b101 & bit_extender_3_out;  // AND_Gate and_5, 3 bits wide
  Multiplexer #(.width(3)) multiplexer_3 (.in0(3'b011), .in1(3'b100), .out(EXEC_next), .sel(CAT0));
  or or_2 (DECODE_next_EXEC, LOAD, STORE, OP_IMM, OP, AUIPC, LUI);
  or or_3 (DECODE_next_CTRL, BRANCH, JALR, JAL);

  assign SR_CLK = CLK;

  // Other names for the same wires on the sheet: EXEC_next_MEM = CAT0; next_S[2:0] = next_state; O[6:0] = opcode;
  //   RAM[31:0] = RAM_output; real_O[4:0] = {CAT, LEN}; VAR[1:0] = real_O; S[2:0] = SR
endmodule

module PC_Controller (
  input  is_fetch,
  input  is_control,
  input  [6:0] opcode,
  input  [2:0] funct3,
  input  [31:0] rs1_data,
  input  [31:0] rs2_data,
  input  [31:0] immediate,
  input  [31:0] pc,
  input  CLK,
  output [31:0] new_pc,
  output WE,
  output pc_CLK
);

  wire and_1_out, BRANCH, CMP_RET, DO_JMP, JAL, JALR;
  wire [0:0] adder_1_out;
  wire [31:0] BASE, OFFSET;

  or or_1 (WE, is_fetch, is_control);
  CMP cmp_1 (.funct3(funct3), .A(rs1_data), .B(rs2_data), .result(CMP_RET));
  Adder #(.width(32)) adder_1 (.a(BASE), .b(OFFSET), .out({new_pc[31:1], adder_1_out[0]}));  // open: cin, cout
  Decoder #(.select(2)) decoder_1 (
    .out0(BRANCH), .out1(JALR), .out2(JAL), .sel(opcode[3:2]), .en(is_control));  // open: out3
  Multiplexer #(.width(32)) multiplexer_1 (.in0(pc), .in1(rs1_data), .out(BASE), .sel(JALR));
  and and_1 (and_1_out, CMP_RET, BRANCH);
  Multiplexer #(.enable("true"), .width(32)) multiplexer_2 (
    .in0(32'h4), .in1(immediate), .out(OFFSET), .sel(DO_JMP), .en(WE));
  or or_2 (DO_JMP, and_1_out, JALR, JAL);

  assign new_pc[0] = 1'b0;
  assign pc_CLK = CLK;

  // Other names for the same wires on the sheet: EN = WE; F3[2:0] = funct3; IMM[31:0] = immediate; O[6:0] = opcode;
  //   CAT[2:0] = opcode[4:2]; RS1[31:0] = rs1_data; RS2[31:0] = rs2_data; S_CTRL = is_control; S_FETCH = is_fetch
endmodule

module RAM_Controller (
  input  S_FETCH,
  input  S_MEM,
  input  [6:0] opcode,
  input  [2:0] funct3,
  input  [31:0] pc,
  input  [31:0] ALUOut,
  input  [31:0] rs2_data,
  input  CLK,
  output [2:0] RAM_funct3,
  output RAM_output_enable,
  output RAM_write_enable,
  output [31:0] RAM_address,
  output [31:0] RAM_write_data,
  output RAM_CLK
);

  wire and_1_out, is_LOAD;

  or or_1 (RAM_output_enable, S_FETCH, and_1_out);
  and and_1 (and_1_out, is_LOAD, S_MEM);
  not not_1 (is_LOAD, opcode[5]);
  and and_2 (RAM_write_enable, opcode[5], S_MEM);
  Multiplexer #(.width(3)) multiplexer_1 (.in0(funct3), .in1(3'b010), .out(RAM_funct3), .sel(S_FETCH));
  Multiplexer #(.width(32)) multiplexer_2 (.in0(ALUOut), .in1(pc), .out(RAM_address), .sel(S_FETCH));

  assign RAM_CLK = CLK;
  assign RAM_write_data = rs2_data;

  // Other names for the same wires on the sheet: ADDR[31:0] = RAM_address; ALU_O[31:0] = ALUOut; F3[2:0] = funct3;
  //   F3_REAL[2:0] = RAM_funct3; O[6:0] = opcode; is_STORE = opcode[5]; VAR[1:0] = opcode[6:5];
  //   OE = RAM_output_enable; WD[31:0] = rs2_data; WE = RAM_write_enable
endmodule

module CMP (
  input  [2:0] funct3,
  input  [31:0] A,
  input  [31:0] B,
  output result
);

  wire CMP_RET, EQ, LT, LTU;

  Comparator #(.width(32)) comparator_1 (.a(A), .b(B), .eq(EQ), .lt(LT));  // open: gt
  Multiplexer #(.select(2)) multiplexer_1 (.in0(EQ), .in1(1'b0), .in2(LT), .in3(LTU), .out(CMP_RET), .sel(funct3[2:1]));
  Comparator #(.mode("unsigned"), .width(32)) comparator_2 (.a(A), .b(B), .lt(LTU));  // open: gt, eq
  xor xor_1 (result, CMP_RET, funct3[0]);

  // Other names for the same wires on the sheet: F3[2:0] = funct3; INV = funct3[0]; SEL[1:0] = funct3[2:1];
  //   FIN_RET = result
endmodule

module Register_File (
  input  write_enable,
  input  [4:0] write_address,
  input  [4:0] output_address_0,
  input  [4:0] output_address_1,
  input  [31:0] write_data,
  input  CLK,
  output [31:0] output_data_0,
  output [31:0] output_data_1
);

  wire WE00, WE01, WE02, WE03, WE04, WE05, WE06, WE07, WE08, WE09, WE10, WE11, WE12, WE13, WE14, WE15, WE16,
       WE17, WE18, WE19, WE20, WE21, WE22, WE23, WE24, WE25, WE26, WE27, WE28, WE29, WE30, WE31;
  wire [31:0] multiplexer_1_out, multiplexer_2_out, multiplexer_3_out, multiplexer_4_out, multiplexer_6_out,
       multiplexer_7_out, multiplexer_8_out, multiplexer_9_out, Q00, Q01, Q02, Q03, Q04, Q05, Q06, Q07, Q08,
       Q09, Q10, Q11, Q12, Q13, Q14, Q15, Q16, Q17, Q18, Q19, Q20, Q21, Q22, Q23, Q24, Q25, Q26, Q27, Q28,
       Q29, Q30, Q31;

  Register #(.width(32)) x00 (.D(write_data), .en(WE00), .clk(CLK), .Q(Q00), .clr(1'b1));
  Register #(.width(32)) x08 (.D(write_data), .en(WE08), .clk(CLK), .Q(Q08));  // open: clr
  Register #(.width(32)) x16 (.D(write_data), .en(WE16), .clk(CLK), .Q(Q16));  // open: clr
  Register #(.width(32)) x24 (.D(write_data), .en(WE24), .clk(CLK), .Q(Q24));  // open: clr
  Decoder #(.select(5)) decoder_1 (
    .out0(WE00), .out1(WE01), .out2(WE02), .out3(WE03), .out4(WE04), .out5(WE05), .out6(WE06), .out7(WE07),
    .out8(WE08), .out9(WE09), .out10(WE10), .out11(WE11), .out12(WE12), .out13(WE13), .out14(WE14),
    .out15(WE15), .out16(WE16), .out17(WE17), .out18(WE18), .out19(WE19), .out20(WE20), .out21(WE21),
    .out22(WE22), .out23(WE23), .out24(WE24), .out25(WE25), .out26(WE26), .out27(WE27), .out28(WE28),
    .out29(WE29), .out30(WE30), .out31(WE31), .sel(write_address), .en(write_enable));
  Register #(.width(32)) x01 (.D(write_data), .en(WE01), .clk(CLK), .Q(Q01));  // open: clr
  Register #(.width(32)) x09 (.D(write_data), .en(WE09), .clk(CLK), .Q(Q09));  // open: clr
  Register #(.width(32)) x17 (.D(write_data), .en(WE17), .clk(CLK), .Q(Q17));  // open: clr
  Register #(.width(32)) x25 (.D(write_data), .en(WE25), .clk(CLK), .Q(Q25));  // open: clr
  Register #(.width(32)) x02 (.D(write_data), .en(WE02), .clk(CLK), .Q(Q02));  // open: clr
  Register #(.width(32)) x10 (.D(write_data), .en(WE10), .clk(CLK), .Q(Q10));  // open: clr
  Register #(.width(32)) x18 (.D(write_data), .en(WE18), .clk(CLK), .Q(Q18));  // open: clr
  Register #(.width(32)) x26 (.D(write_data), .en(WE26), .clk(CLK), .Q(Q26));  // open: clr
  Multiplexer #(.select(3), .width(32)) multiplexer_1 (
    .in0(Q08), .in1(Q09), .in2(Q10), .in3(Q11), .in4(Q12), .in5(Q13), .in6(Q14), .in7(Q15),
    .out(multiplexer_1_out), .sel(output_address_0[2:0]));
  Multiplexer #(.select(3), .width(32)) multiplexer_2 (
    .in0(Q24), .in1(Q25), .in2(Q26), .in3(Q27), .in4(Q28), .in5(Q29), .in6(Q30), .in7(Q31),
    .out(multiplexer_2_out), .sel(output_address_0[2:0]));
  Register #(.width(32)) x03 (.D(write_data), .en(WE03), .clk(CLK), .Q(Q03));  // open: clr
  Register #(.width(32)) x11 (.D(write_data), .en(WE11), .clk(CLK), .Q(Q11));  // open: clr
  Register #(.width(32)) x19 (.D(write_data), .en(WE19), .clk(CLK), .Q(Q19));  // open: clr
  Register #(.width(32)) x27 (.D(write_data), .en(WE27), .clk(CLK), .Q(Q27));  // open: clr
  Register #(.width(32)) x04 (.D(write_data), .en(WE04), .clk(CLK), .Q(Q04));  // open: clr
  Register #(.width(32)) x12 (.D(write_data), .en(WE12), .clk(CLK), .Q(Q12));  // open: clr
  Register #(.width(32)) x20 (.D(write_data), .en(WE20), .clk(CLK), .Q(Q20));  // open: clr
  Register #(.width(32)) x28 (.D(write_data), .en(WE28), .clk(CLK), .Q(Q28));  // open: clr
  Multiplexer #(.select(3), .width(32)) multiplexer_3 (
    .in0(Q00), .in1(Q01), .in2(Q02), .in3(Q03), .in4(Q04), .in5(Q05), .in6(Q06), .in7(Q07),
    .out(multiplexer_3_out), .sel(output_address_0[2:0]));
  Multiplexer #(.select(3), .width(32)) multiplexer_4 (
    .in0(Q16), .in1(Q17), .in2(Q18), .in3(Q19), .in4(Q20), .in5(Q21), .in6(Q22), .in7(Q23),
    .out(multiplexer_4_out), .sel(output_address_0[2:0]));
  Multiplexer #(.select(2), .width(32)) multiplexer_5 (
    .in0(multiplexer_3_out), .in1(multiplexer_1_out), .in2(multiplexer_4_out), .in3(multiplexer_2_out),
    .out(output_data_0), .sel(output_address_0[4:3]));
  Register #(.width(32)) x05 (.D(write_data), .en(WE05), .clk(CLK), .Q(Q05));  // open: clr
  Register #(.width(32)) x13 (.D(write_data), .en(WE13), .clk(CLK), .Q(Q13));  // open: clr
  Register #(.width(32)) x21 (.D(write_data), .en(WE21), .clk(CLK), .Q(Q21));  // open: clr
  Register #(.width(32)) x29 (.D(write_data), .en(WE29), .clk(CLK), .Q(Q29));  // open: clr
  Register #(.width(32)) x06 (.D(write_data), .en(WE06), .clk(CLK), .Q(Q06));  // open: clr
  Register #(.width(32)) x14 (.D(write_data), .en(WE14), .clk(CLK), .Q(Q14));  // open: clr
  Register #(.width(32)) x22 (.D(write_data), .en(WE22), .clk(CLK), .Q(Q22));  // open: clr
  Register #(.width(32)) x30 (.D(write_data), .en(WE30), .clk(CLK), .Q(Q30));  // open: clr
  Multiplexer #(.select(3), .width(32)) multiplexer_6 (
    .in0(Q08), .in1(Q09), .in2(Q10), .in3(Q11), .in4(Q12), .in5(Q13), .in6(Q14), .in7(Q15),
    .out(multiplexer_6_out), .sel(output_address_1[2:0]));
  Multiplexer #(.select(3), .width(32)) multiplexer_7 (
    .in0(Q24), .in1(Q25), .in2(Q26), .in3(Q27), .in4(Q28), .in5(Q29), .in6(Q30), .in7(Q31),
    .out(multiplexer_7_out), .sel(output_address_1[2:0]));
  Register #(.width(32)) x07 (.D(write_data), .en(WE07), .clk(CLK), .Q(Q07));  // open: clr
  Register #(.width(32)) x15 (.D(write_data), .en(WE15), .clk(CLK), .Q(Q15));  // open: clr
  Register #(.width(32)) x23 (.D(write_data), .en(WE23), .clk(CLK), .Q(Q23));  // open: clr
  Register #(.width(32)) x31 (.D(write_data), .en(WE31), .clk(CLK), .Q(Q31));  // open: clr
  Multiplexer #(.select(3), .width(32)) multiplexer_8 (
    .in0(Q00), .in1(Q01), .in2(Q02), .in3(Q03), .in4(Q04), .in5(Q05), .in6(Q06), .in7(Q07),
    .out(multiplexer_8_out), .sel(output_address_1[2:0]));
  Multiplexer #(.select(3), .width(32)) multiplexer_9 (
    .in0(Q16), .in1(Q17), .in2(Q18), .in3(Q19), .in4(Q20), .in5(Q21), .in6(Q22), .in7(Q23),
    .out(multiplexer_9_out), .sel(output_address_1[2:0]));
  Multiplexer #(.select(2), .width(32)) multiplexer_10 (
    .in0(multiplexer_8_out), .in1(multiplexer_6_out), .in2(multiplexer_9_out), .in3(multiplexer_7_out),
    .out(output_data_1), .sel(output_address_1[4:3]));

  // Other names for the same wires on the sheet: D[31:0] = write_data; OA0[4:0] = output_address_0;
  //   OA0_LOW[2:0] = output_address_0[2:0]; OA0_HI[1:0] = output_address_0[4:3]; OA1[4:0] = output_address_1;
  //   OA1_LOW[2:0] = output_address_1[2:0]; OA1_HI[1:0] = output_address_1[4:3]; OD0[31:0] = output_data_0;
  //   OD1[31:0] = output_data_1; WA[4:0] = write_address; WE = write_enable
endmodule
